# Fritzing sketch s3smsf (saved by Fritzing 0.9.5d)
breadboards: 2

parts:
  GSM_SIM_GPSR_SMS_SIM900_SIM1 = SIM800L [package=THT]
  Power_5v_2A = Power plug [part_number="USB Type-C"]
  OLED_I2C1 = OLED 128x64 I2C Monochrome Display
  U1 = ESP32-38PinWide [part_number=ESP32-38PinWide]
  D1 = P1000K [part_number=RL207]
  C1 = Electrolytic Capacitor [capacitance=0pF part_number=4700uF,16v package="100 mil [THT, electrolytic]"]

nets:
  5V: GSM_SIM_GPSR_SMS_SIM900_SIM1.5V, Power_5v_2A.VCC, D1.anode, C1.+
  N1: GSM_SIM_GPSR_SMS_SIM900_SIM1.GND#1, Power_5v_2A.GND, U1.GPIO11, C1.-
  N2: GSM_SIM_GPSR_SMS_SIM900_SIM1.SIM_TXD, U1.GPIO27
  N3: GSM_SIM_GPSR_SMS_SIM900_SIM1.SIM_RXD, U1.GPIO25
  N4: OLED_I2C1.SDA, U1.GPIO21
  N5: OLED_I2C1.SCK, U1.GPIO22
  N6: U1.VIN, D1.cathode

custom parts:
  ESP32-38PinWide: Generic 38-Pin ESP32 with wide format (only access to one side of pins on a breadboard) based on Stephen Lilley's HiLetgo ESP-WROOM-32 ESP32 ESP-32S Development Board.
